# Fritzing sketch motor_dc (saved by Fritzing 0.9.3b)
breadboards: 1

parts:
  Componente1 = iceZUM Alhambra
  R2 = Resistor [tolerance=±5% resistance=220 package="0805 [SMD]"]
  S1 = Pushbutton [package="[THT]"]
  S2 = Pushbutton [package="[THT]"]
  R3 = Resistor [tolerance=±5% resistance=220 package="0805 [SMD]"]
  L298N2 = L298N DC motor driver
  U2 = LIPO-2000mAh [package=lipo-2000]
  M3 = DC Motor
  S3 = Pushbutton [package="[THT]"]
  R4 = Resistor [tolerance=±5% resistance=220 package="0805 [SMD]"]

nets:
  N1: Componente1.D0, Componente1.V0, L298N2.ENA
  N2: Componente1.D1, Componente1.V1, L298N2.IN1
  N3: Componente1.D2, Componente1.V2, L298N2.IN2
  N4: Componente1.D11, Componente1.D12, Componente1.D13, Componente1.V13, Componente1.5V, S1.Pin_1, S1.Pin_2, S2.Pin_1, S2.Pin_2, S3.Pin_1, S3.Pin_2
  GND: Componente1.V8, Componente1.GD2, Componente1.GND, R2.Pin_0, R3.Pin_0, L298N2.GND, U2.-, R4.Pin_0
  N5: R2.Pin_1, S1.Pin_3, S1.Pin_4
  N6: S2.Pin_3, S2.Pin_4, R3.Pin_1
  N7: L298N2.OUT1, M3.pin_2
  N8: L298N2.OUT2, M3.pin_1
  N9: L298N2.12V, U2.+
  N10: S3.Pin_3, S3.Pin_4, R4.Pin_1

custom parts:
  iceZUM Alhambra: Arduino/zum compatible Open FPGA electronic board. Synthesize hardware easily, using only open source tools
  L298N DC motor driver: 2x DC motor driver with 78M05 positive voltage regulator (7..35 V) L298N: max 46 V, 2 A Set 5 V Enable jumper to enable 5 V regultor (needed for the L298N) and +5 V output at screw terminal or supply external +5 V at screw terminal Set ENA and/or ENB to +5 V to enable motor permanently or supply ENA and/or ENB with PWM signal IN1 and IN2 set rotation directory for motor A (OUT1/OUT2) IN2 and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
