# Fritzing sketch lcd (saved by Fritzing 0.9.3b)
breadboards: 1

parts:
  R1 = Rotary Potentiometer (Small) [maximum_resistance=100kΩ package=THT]
  U2 = LCD-16X2 [package=lcd-16x2]
  Componente1 = iceZUM Alhambra
  R2 = Resistor [tolerance=±5% resistance=1k package="0805 [SMD]"]

nets:
  VDD: R1.leg1, U2.VDD, Componente1.5V, R2.Pin_0
  N1: R1.wiper, U2.VO
  VSS: R1.leg2, U2.VSS, Componente1.GD0, Componente1.GND
  N2: U2.RS, Componente1.D13
  N3: U2.R_W, Componente1.D12
  N4: U2.E, Componente1.D11
  N5: U2.DB0, Componente1.D0, Componente1.V0
  N6: U2.DB1, Componente1.D1, Componente1.V1
  N7: U2.DB2, Componente1.D2, Componente1.V2
  N8: U2.DB3, Componente1.D3, Componente1.V3
  N9: U2.DB4, Componente1.D4, Componente1.V4
  N10: U2.DB5, Componente1.D5, Componente1.V5
  N11: U2.DB6, Componente1.D6, Componente1.V6
  N12: U2.DB7, Componente1.D7

custom parts:
  iceZUM Alhambra: Arduino/zum compatible Open FPGA electronic board. Synthesize hardware easily, using only open source tools
