# Fritzing sketch button_debouncer (saved by Fritzing 0.9.3b)
breadboards: 1

parts:
  Componente1 = iceZUM Alhambra
  R2 = Resistor [tolerance=±5% resistance=220 package="0805 [SMD]"]
  S1 = Pushbutton [package="[THT]"]
  LED1 = smd LED [color="Red (633nm)" package="0603 [SMD]"]
  R3 = Resistor [tolerance=±5% resistance=220 package="0805 [SMD]"]

nets:
  N1: Componente1.D12, R3.Pin_1
  N2: Componente1.D13, Componente1.5V, S1.Pin_1, S1.Pin_2
  N3: Componente1.GD3, Componente1.GND, R2.Pin_0, LED1.cathode
  N4: R2.Pin_1, S1.Pin_3, S1.Pin_4
  N5: LED1.anode, R3.Pin_0

custom parts:
  iceZUM Alhambra: Arduino/zum compatible Open FPGA electronic board. Synthesize hardware easily, using only open source tools
